# Fritzing sketch Circuit (saved by Fritzing 0.9.3b)

parts:
  WeMos_D1_Mini1 = WeMos D1 Mini
  Part1 = NRF24L01+ Breakout Board
  U1 = ESP32-HiLetgo [part_number=ESP32S-HiLetgo]
  Part2 = NRF24L01+ Breakout Board
  C1 = Capacitor Polarized [package=cpol-radial-100uf-25v]
  C2 = Capacitor Polarized [package=cpol-radial-100uf-25v]

nets:
  3V3: WeMos_D1_Mini1.3V3, Part2.VCC
  N1: WeMos_D1_Mini1.D0, Part2.CE
  N2: WeMos_D1_Mini1.D5, Part2.SCK
  N3: WeMos_D1_Mini1.D6, Part2.MISO
  N4: WeMos_D1_Mini1.D7, Part2.MOSI
  N5: WeMos_D1_Mini1.D8, Part2.CS
  N6: WeMos_D1_Mini1.G, Part2.GND, C2.-
  N7: Part1.GND, U1.connector20, C1.-
  N8: Part1.VCC, U1.connector19, C1.+
  N9: Part1.CE, U1.connector25
  N10: Part1.CS, U1.connector28
  N11: Part1.SCK, U1.connector29
  N12: Part1.MOSI, U1.connector36
  N13: Part1.MISO, U1.connector30
